# Fritzing sketch schematic (saved by Fritzing 0.9.3b)
breadboards: 1

parts:
  Part2 = Arduino MP3 Player Shield
  Part3 = Arduino Uno (Rev3)
  LCD1 = LCD screen
  S1 = Pushbutton [package="[THT]"]
  R1 = TRIMPOT [package=trimpot_pth_s3_lock]
  part = Resistor [tolerance=±5% resistance=330 package=THT]
  RGB_LED = RGB LED (com. cathode, rgb) [package="5 mm [THT]"]
  part_2 = Resistor [tolerance=±5% resistance=10k package=THT]
  U1 = mystery part, 7 pins [chip_label="RGB Sensor"]

nets:
  N1: Part2.MP3-DREQ, Part3.D2
  N2: Part2.5V-MIDI-RX, Part3.D3_PWM
  N3: Part2.5V-GPIO1, Part3.D4
  N4: Part2.D5, Part3.D5_PWM
  N5: Part2.D10, Part3.D10_PWM/SS
  N6: Part2.5V-MOSI, Part3.D11_PWM/MOSI
  N7: Part2.MISO, Part3.D12/MISO
  N8: Part2.5V-SCK, Part3.D13/SCK
  N9: Part3.A0, RGB_LED.red_anode
  N10: Part3.A1, RGB_LED.green_anode
  N11: Part3.A2, RGB_LED.blue_anode
  N12: Part3.A3, S1.Pin_1, S1.Pin_2, part_2.Pin_1
  N13: Part3.A4/SDA, U1.pin3
  N14: Part3.A5/SCL, U1.pin4
  N15: Part3.D8, LCD1.DB5
  N16: Part3.D9_PWM, LCD1.DB4
  N17: Part3.D0/RX, LCD1.E
  N18: Part3.D1/TX, LCD1.RS
  N19: Part3.D6_PWM, LCD1.DB7
  N20: Part3.D7, LCD1.DB6
  5V: Part3.5V, LCD1.VDD, R1.CW, part.Pin_0, part_2.Pin_0, U1.pin7
  GND: Part3.GND, LCD1.VSS, LCD1.R/W, LCD1.LED-, S1.Pin_3, S1.Pin_4, R1.CCW, RGB_LED.common_cathode, U1.pin6
  N21: LCD1.V0, R1.WIPER
  N22: LCD1.LED+, part.Pin_1
